// Logisim project cpu_alt.circ as structural Verilog: 6 circuits, main circuit main
module main (
);

  wire bus_buffer_1_select, bus_buffer_2_select, button_1_out, clock_1_out, cpu_1_read, cpu_1_write, or_1_out;
  wire [15:0] bus_buffer_1_mapped_address, bus_buffer_2_mapped_address, controlled_buffer_1_out,
       controlled_buffer_2_out, cpu_1_address_bus, cpu_1_data_out;

  Clock clock_1 (.out(clock_1_out));
  Button button_1 (.out(button_1_out));
  or or_1 (or_1_out, button_1_out, clock_1_out);
  CPU cpu_1 (
    .CLK(or_1_out), .Address_Bus(cpu_1_address_bus), .Data_Out(cpu_1_data_out), .Read(cpu_1_read),
    .Write(cpu_1_write), .Data_In(controlled_buffer_2_out));
  assign controlled_buffer_1_out = cpu_1_write ? cpu_1_data_out : 16'bz;  // Controlled_Buffer controlled_buffer_1
  assign controlled_buffer_2_out = cpu_1_read ? controlled_buffer_1_out : 16'bz;  // Controlled_Buffer controlled_buffer_2
  bus_buffer bus_buffer_1 (
    .Low_Address({16{1'b0}}), .High_Address(16'h3ff), .Mapped_Address(bus_buffer_1_mapped_address),
    .Select(bus_buffer_1_select), .Address_Bus(cpu_1_address_bus));
  ROM #(.addrWidth(16), .dataWidth(16)) rom_1 (
    .addr(bus_buffer_1_mapped_address), .data(controlled_buffer_1_out), .sel(bus_buffer_1_select));
  bus_buffer bus_buffer_2 (
    .Low_Address(16'h400), .High_Address(16'h7ff), .Mapped_Address(bus_buffer_2_mapped_address),
    .Select(bus_buffer_2_select), .Address_Bus(cpu_1_address_bus));
  RAM #(.addrWidth(16), .dataWidth(16)) ram_1 (
    .addr(bus_buffer_2_mapped_address), .data(controlled_buffer_1_out), .sel(bus_buffer_2_select),
    .clk(or_1_out), .ld(cpu_1_read));  // open: clr

  // Notes on the sheet:
  //   contents of rom_1 (hex, n*v repeats v):
  //   c00 beef c40 400 1008 2
endmodule

// REGISTERS
module register_file (
  input  WRITE,
  input  [2:0] Sel_RD,
  input  [2:0] Sel_RS,
  input  [2:0] Sel_RT,
  input  [15:0] Data,
  input  CLK,
  output [15:0] RS,
  output [15:0] RT
);

  wire decoder_1_out0, decoder_1_out1, decoder_1_out2, decoder_1_out3, decoder_1_out4, decoder_1_out5,
       decoder_1_out6, decoder_1_out7;
  wire [15:0] register_1_q, register_2_q, register_3_q, register_4_q, register_5_q, register_6_q,
       register_7_q, register_8_q;

  Decoder #(.select(3), .disabled(0)) decoder_1 (
    .out0(decoder_1_out0), .out1(decoder_1_out1), .out2(decoder_1_out2), .out3(decoder_1_out3),
    .out4(decoder_1_out4), .out5(decoder_1_out5), .out6(decoder_1_out6), .out7(decoder_1_out7), .sel(Sel_RD),
    .en(WRITE));
  Register #(.width(16), .trigger("falling")) register_1 (
    .D(Data), .en(decoder_1_out0), .Q(register_1_q), .clk(CLK));  // open: clr
  Register #(.width(16), .trigger("falling")) register_2 (
    .D(Data), .en(decoder_1_out1), .Q(register_2_q), .clk(CLK));  // open: clr
  Register #(.width(16), .trigger("falling")) register_3 (
    .D(Data), .en(decoder_1_out2), .Q(register_3_q), .clk(CLK));  // open: clr
  Register #(.width(16), .trigger("falling")) register_4 (
    .D(Data), .en(decoder_1_out3), .Q(register_4_q), .clk(CLK));  // open: clr
  Register #(.width(16), .trigger("falling")) register_5 (
    .D(Data), .en(decoder_1_out4), .Q(register_5_q), .clk(CLK));  // open: clr
  Register #(.width(16), .trigger("falling")) register_6 (
    .D(Data), .en(decoder_1_out5), .Q(register_6_q), .clk(CLK));  // open: clr
  Register #(.width(16), .trigger("falling")) register_7 (
    .D(Data), .en(decoder_1_out6), .Q(register_7_q), .clk(CLK));  // open: clr
  Register #(.width(16), .trigger("falling")) register_8 (
    .D(Data), .en(decoder_1_out7), .Q(register_8_q), .clk(CLK));  // open: clr
  Multiplexer #(.select(3), .width(16), .enable("false")) multiplexer_1 (
    .in0(register_1_q), .in1(register_2_q), .in2(register_3_q), .in3(register_4_q), .in4(register_5_q),
    .in5(register_6_q), .in6(register_7_q), .in7(register_8_q), .out(RS), .sel(Sel_RS));
  Multiplexer #(.select(3), .width(16), .enable("false")) multiplexer_2 (
    .in0(register_1_q), .in1(register_2_q), .in2(register_3_q), .in3(register_4_q), .in4(register_5_q),
    .in5(register_6_q), .in6(register_7_q), .in7(register_8_q), .out(RT), .sel(Sel_RT));
endmodule

module ALU (
  input  [3:0] Operation,
  input  [15:0] A,
  input  [15:0] B,
  output [15:0] Q,
  output Zero
);

  wire [15:0] adder_1_out, and_1_out, not_1_out, not_2_out, or_1_out, shifter_1_out, shifter_2_out,
       subtractor_1_out, xor_1_out;

  Adder #(.width(16)) adder_1 (.a(A), .b(B), .out(adder_1_out), .cin(1'b0));  // open: cout
  Subtractor #(.width(16)) subtractor_1 (.a(A), .b(B), .out(subtractor_1_out), .bin(1'b0));  // open: bout
  assign and_1_out = A & B;  // AND_Gate and_1, 16 bits wide
  assign or_1_out = A | B;  // OR_Gate or_1, 16 bits wide
  assign xor_1_out = A ^ B;  // XOR_Gate xor_1, 16 bits wide
  Shifter #(.width(16)) shifter_1 (.in(A), .\dist (B[3:0]), .out(shifter_1_out));
  Shifter #(.width(16), .shift("lr")) shifter_2 (.in(A), .\dist (B[3:0]), .out(shifter_2_out));
  assign not_1_out = ~and_1_out;  // NOT_Gate not_1, 16 bits wide
  assign not_2_out = ~or_1_out;  // NOT_Gate not_2, 16 bits wide
  nor nor_1 (Zero, Q[15], Q[14], Q[13], Q[12], Q[11], Q[10], Q[9], Q[8], Q[6], Q[5], Q[4], Q[3], Q[2], Q[1], Q[0], Q[7]);
  Multiplexer #(.select(4), .width(16), .disabled(0), .enable("false")) multiplexer_1 (
    .in0(adder_1_out), .in1(subtractor_1_out), .in2(and_1_out), .in3(not_1_out), .in4(or_1_out),
    .in5(not_2_out), .in6(xor_1_out), .in8(shifter_1_out), .in9(shifter_2_out), .in10(A), .in11(B), .out(Q),
    .sel(Operation));  // open: in7, in12, in13, in14, in15

  // Notes on the sheet:
  //   Operation: pull=down
  //   A: pull=down
  //   Zero: pull=down
  //   B: pull=down
  //   Q: pull=down
endmodule

module CPU (
  input  CLK,
  input  [15:0] Data_In,
  output [15:0] Address_Bus,
  output [15:0] Data_Out,
  output Read,
  output Write
);

  wire control_1_a_select, control_1_alu_op_select, control_1_flags_write, control_1_imm_write,
       control_1_ir_write, control_1_pc_write, control_1_register_write;
  wire [1:0] ALU_FLAGS_q, control_1_address_select, control_1_b_select, control_1_pc_select,
       control_1_rd_input_select;
  wire [1:1] alu_1_zero;
  wire [2:0] IR_q, IR_q_2, IR_q_3;
  wire [3:0] control_1_alu_op, multiplexer_4_out;
  wire [6:0] IR_q_4;
  wire [15:0] alu_1_q, IMM_q, multiplexer_2_out, multiplexer_3_out, multiplexer_5_out, multiplexer_6_out,
       PC_q, register_file_1_rs;

  control control_1 (
    .ALU_OP(control_1_alu_op), .A_select(control_1_a_select), .RD_input_select(control_1_rd_input_select),
    .PC_select(control_1_pc_select), .B_select(control_1_b_select),
    .Address_select(control_1_address_select), .Flags_write(control_1_flags_write),
    .IR_write(control_1_ir_write), .IMM_write(control_1_imm_write),
    .register_write(control_1_register_write), .write(Write), .read(Read), .CLK(CLK), .Opcode(IR_q_4),
    .Zero(ALU_FLAGS_q[1]), .Negative(ALU_FLAGS_q[0]), .PC_write(control_1_pc_write),
    .ALU_OP_select(control_1_alu_op_select));
  Register #(.width(16), .trigger("falling")) IMM (
    .D(Data_In), .en(control_1_imm_write), .Q(IMM_q), .clk(CLK));  // open: clr
  Multiplexer #(.select(2), .width(16), .disabled(0), .enable("false")) multiplexer_1 (
    .in0(PC_q), .in1(register_file_1_rs), .in2(alu_1_q), .in3(IMM_q), .out(Address_Bus),
    .sel(control_1_address_select));
  Multiplexer #(.select(2), .width(16), .disabled(0), .enable("false")) multiplexer_2 (
    .in0(Data_In), .in1(IMM_q), .in2(alu_1_q), .out(multiplexer_2_out), .sel(control_1_rd_input_select));  // open: in3
  register_file register_file_1 (
    .Data(multiplexer_2_out), .RS(register_file_1_rs), .RT(Data_Out), .WRITE(control_1_register_write),
    .Sel_RD(IR_q_3), .Sel_RS(IR_q_2), .Sel_RT(IR_q), .CLK(CLK));
  Multiplexer #(.select(2), .width(16), .disabled(0), .enable("false")) multiplexer_3 (
    .in0(alu_1_q), .in1(register_file_1_rs), .in2(Data_In), .in3(IMM_q), .out(multiplexer_3_out),
    .sel(control_1_pc_select));
  Register #(.width(16), .trigger("falling")) IR (
    .D(Data_In), .en(control_1_ir_write), .Q({IR_q_4, IR_q_3, IR_q_2, IR_q}), .clk(CLK));  // open: clr
  Register #(.width(16), .trigger("falling")) PC (
    .D(multiplexer_3_out), .en(control_1_pc_write), .Q(PC_q), .clk(CLK));  // open: clr
  Multiplexer #(.width(4), .disabled(0), .enable("false")) multiplexer_4 (
    .in0(control_1_alu_op), .in1(IR_q_4[3:0]), .out(multiplexer_4_out), .sel(control_1_alu_op_select));
  Multiplexer #(.width(16), .disabled(0), .enable("false")) multiplexer_5 (
    .in0(register_file_1_rs), .in1(PC_q), .out(multiplexer_5_out), .sel(control_1_a_select));
  Multiplexer #(.select(2), .width(16), .disabled(0), .enable("false")) multiplexer_6 (
    .in0(Data_Out), .in1(16'h1), .in2(16'h2), .in3(IMM_q), .out(multiplexer_6_out), .sel(control_1_b_select));
  ALU alu_1 (
    .A(multiplexer_5_out), .B(multiplexer_6_out), .Q(alu_1_q), .Operation(multiplexer_4_out),
    .Zero(alu_1_zero[1]));
  Register #(.width(2), .trigger("falling")) ALU_FLAGS (
    .D({alu_1_zero[1], alu_1_q[15]}), .en(control_1_flags_write), .Q(ALU_FLAGS_q), .clk(CLK));  // open: clr

  // Notes on the sheet:
  //   Write: pull=down
  //   Read: pull=down
  //   Data_Out: pull=down
  //   Data_In: pull=down
endmodule

// CONTROL
module control (
  input  CLK,
  input  [6:0] Opcode,
  input  Zero,
  input  Negative,
  output [3:0] ALU_OP,
  output ALU_OP_select,
  output A_select,
  output [1:0] RD_input_select,
  output [1:0] PC_select,
  output [1:0] B_select,
  output [1:0] Address_select,
  output Flags_write,
  output PC_write,
  output IR_write,
  output IMM_write,
  output register_write,
  output write,
  output read
);

  wire [4:0] State_q;
  wire [7:0] rom_1_data;
  wire [31:21] rom_2_data;

  ROM #(.addrWidth(14)) rom_1 (.addr({Opcode, Zero, Negative, State_q}), .data(rom_1_data));  // open: sel
  Register #(.width(5)) State (.D(rom_1_data[4:0]), .Q(State_q), .clk(CLK));  // open: en, clr
  ROM #(.addrWidth(5), .dataWidth(32)) rom_2 (
    .addr(State_q),
    .data({rom_2_data, ALU_OP, ALU_OP_select, A_select, RD_input_select, PC_select, B_select, Address_select, Flags_write, PC_write, IR_write, IMM_write, register_write, write, read}));  // open: sel

  // Notes on the sheet:
  //   Zero: pull=down
  //   Opcode: pull=down
  //   Address_select: pull=down
  //   CLK: pull=down
  //   PC_write: pull=down
  //   Flags_write: pull=down
  //   IR_write: pull=down
  //   B_select: pull=down
  //   register_write: pull=down
  //   ALU_OP_select: pull=down
  //   ALU_OP: pull=down
  //   A_select: pull=down
  //   write: pull=down
  //   RD_input_select: pull=down
  //   IMM_write: pull=down
  //   PC_select: pull=down
  //   Negative: pull=down
  //   read: pull=down
  //   Decision ROM
  //   contents of rom_1 (hex, n*v repeats v):
  //   1 2 1 1 4 3 1 3 3 1 1 1 2 2 e f 3 3 2 3 2 15 16 17 18 19 1a 1b 1c 1d 1e 1f 1 2 1 1 4 3 1 3 3 1 1 1 2
  //   2 e f 3 3 2 3 2 15 16 17 18 19 1a 1b 1c 1d 1e 1f 1 2 1 1 4 3 1 3 3 1 1 1 2 2 e f 3 3 2 3 2 15 16 17
  //   18 19 1a 1b 1c 1d 1e 1f 1 2 1 1 4 3 1 3 3 1 1 1 2 2 e f 3 3 2 3 2 15 16 17 18 19 1a 1b 1c 1d 1e 1f 0
  //   1 2 3 4 5 6 7 8 9 a b c d e f 10 11 12 13 14 15 16 17 18 19 1a 1b 1c 1d 1e 1f 0 1 2 3 4 5 6 7 8 9 a
  //   b c d e f 10 11 12 13 14 15 16 17 18 19 1a 1b 1c 1d 1e 1f 0 1 2 3 4 5 6 7 8 9 a b c d e f 10 11 12
  //   13 14 15 16 17 18 19 1a 1b 1c 1d 1e 1f 0 1 2 3 4 5 6 7 8 9 a b c d e f 10 11 12 13 14 15 16 17 18 19
  //   1a 1b 1c 1d 1e 1f 0 1 2 3 4 5 6 7 8 9 a b c d e f 10 11 12 13 14 15 16 17 18 19 1a 1b 1c 1d 1e 1f 0
  //   1 2 3 4 5 6 7 8 9 a b c d e f 10 11 12 13 14 15 16 17 18 19 1a 1b 1c 1d 1e 1f 0 1 2 3 4 5 6 7 8 9 a
  //   b c d e f 10 11 12 13 14 15 16 17 18 19 1a 1b 1c 1d 1e 1f 0 1 2 3 4 5 6 7 8 9 a b c d e f 10 11 12
  //   13 14 15 16 17 18 19 1a 1b 1c 1d 1e 1f 0 1 2 3 4 5 6 7 8 9 a b c d e f 10 11 12 13 14 15 16 17 18 19
  //   1a 1b 1c 1d 1e 1f 0 1 2 3 4 5 6 7 8 9 a b c d e f 10 11 12 13 14 15 16 17 18 19 1a 1b 1c 1d 1e 1f 0
  //   1 2 3 4 5 6 7 8 9 a b c d e f 10 11 12 13 14 15 16 17 18 19 1a 1b 1c 1d 1e 1f 0 1 2 3 4 5 6 7 8 9 a
  //   b c d e f 10 11 12 13 14 15 16 17 18 19 1a 1b 1c 1d 1e 1f 1 c 1 1 4 3 1 3 3 1 1 1 2 2 e f 3 3 2 3 2
  //   15 16 17 18 19 1a 1b 1c 1d 1e 1f 1 c 1 1 4 3 1 3 3 1 1 1 2 2 e f 3 3 2 3 2 15 16 17 18 19 1a 1b 1c
  //   1d 1e 1f 1 c 1 1 4 3 1 3 3 1 1 1 2 2 e f 3 3 2 3 2 15 16 17 18 19 1a 1b 1c 1d 1e 1f 1 c 1 1 4 3 1 3
  //   3 1 1 1 2 2 e f 3 3 2 3 2 15 16 17 18 19 1a 1b 1c 1d 1e 1f 1 d 1 1 4 3 1 3 3 1 1 1 2 2 e f 3 3 2 3 2
  //   15 16 17 18 19 1a 1b 1c 1d 1e 1f 1 d 1 1 4 3 1 3 3 1 1 1 2 2 e f 3 3 2 3 2 15 16 17 18 19 1a 1b 1c
  //   1d 1e 1f 1 d 1 1 4 3 1 3 3 1 1 1 2 2 e f 3 3 2 3 2 15 16 17 18 19 1a 1b 1c 1d 1e 1f 1 d 1 1 4 3 1 3
  //   3 1 1 1 2 2 e f 3 3 2 3 2 15 16 17 18 19 1a 1b 1c 1d 1e 1f 1 5 1 1 4 3 1 3 3 1 1 1 2 2 e f 3 3 2 3 2
  //   15 16 17 18 19 1a 1b 1c 1d 1e 1f 1 5 1 1 4 3 1 3 3 1 1 1 2 2 e f 3 3 2 3 2 15 16 17 18 19 1a 1b 1c
  //   1d 1e 1f 1 5 1 1 4 3 1 3 3 1 1 1 2 2 e f 3 3 2 3 2 15 16 17 18 19 1a 1b 1c 1d 1e 1f 1 5 1 1 4 3 1 3
  //   3 1 1 1 2 2 e f 3 3 2 3 2 15 16 17 18 19 1a 1b 1c 1d 1e 1f 1 4 1 1 7 3 1 3 3 1 1 1 2 2 e f 3 3 2 3 2
  //   15 16 17 18 19 1a 1b 1c 1d 1e 1f 1 4 1 1 7 3 1 3 3 1 1 1 2 2 e f 3 3 2 3 2 15 16 17 18 19 1a 1b 1c
  //   1d 1e 1f 1 4 1 1 7 3 1 3 3 1 1 1 2 2 e f 3 3 2 3 2 15 16 17 18 19 1a 1b 1c 1d 1e 1f 1 4 1 1 7 3 1 3
  //   3 1 1 1 2 2 e f 3 3 2 3 2 15 16 17 18 19 1a 1b 1c 1d 1e 1f 1 4 1 1 8 3 1 3 3 1 1 1 2 2 e f 3 3 2 3 2
  //   15 16 17 18 19 1a 1b 1c 1d 1e 1f 1 4 1 1 8 3 1 3 3 1 1 1 2 2 e f 3 3 2 3 2 15 16 17 18 19 1a 1b 1c
  //   1d 1e 1f 1 4 1 1 8 3 1 3 3 1 1 1 2 2 e f 3 3 2 3 2 15 16 17 18 19 1a 1b 1c 1d 1e 1f 1 4 1 1 8 3 1 3
  //   3 1 1 1 2 2 e f 3 3 2 3 2 15 16 17 18 19 1a 1b 1c 1d 1e 1f 0 1 2 3 4 5 6 7 8 9 a b c d e f 10 11 12
  //   13 14 15 16 17 18 19 1a 1b 1c 1d 1e 1f 0 1 2 3 4 5 6 7 8 9 a b c d e f 10 11 12 13 14 15 16 17 18 19
  //   1a 1b 1c 1d 1e 1f 0 1 2 3 4 5 6 7 8 9 a b c d e f 10 11 12 13 14 15 16 17 18 19 1a 1b 1c 1d 1e 1f 0
  //   1 2 3 4 5 6 7 8 9 a b c d e f 10 11 12 13 14 15 16 17 18 19 1a 1b 1c 1d 1e 1f 0 1 2 3 4 5 6 7 8 9 a
  //   b c d e f 10 11 12 13 14 15 16 17 18 19 1a 1b 1c 1d 1e 1f 0 1 2 3 4 5 6 7 8 9 a b c d e f 10 11 12
  //   13 14 15 16 17 18 19 1a 1b 1c 1d 1e 1f 0 1 2 3 4 5 6 7 8 9 a b c d e f 10 11 12 13 14 15 16 17 18 19
  //   1a 1b 1c 1d 1e 1f 0 1 2 3 4 5 6 7 8 9 a b c d e f 10 11 12 13 14 15 16 17 18 19 1a 1b 1c 1d 1e 1f 0
  //   1 2 3 4 5 6 7 8 9 a b c d e f 10 11 12 13 14 15 16 17 18 19 1a 1b 1c 1d 1e 1f 0 1 2 3 4 5 6 7 8 9 a
  //   b c d e f 10 11 12 13 14 15 16 17 18 19 1a 1b 1c 1d 1e 1f 0 1 2 3 4 5 6 7 8 9 a b c d e f 10 11 12
  //   13 14 15 16 17 18 19 1a 1b 1c 1d 1e 1f 0 1 2 3 4 5 6 7 8 9 a b c d e f 10 11 12 13 14 15 16 17 18 19
  //   1a 1b 1c 1d 1e 1f 0 1 2 3 4 5 6 7 8 9 a b c d e f 10 11 12 13 14 15 16 17 18 19 1a 1b 1c 1d 1e 1f 0
  //   1 2 3 4 5 6 7 8 9 a b c d e f 10 11 12 13 14 15 16 17 18 19 1a 1b 1c 1d 1e 1f 0 1 2 3 4 5 6 7 8 9 a
  //   b c d e f 10 11 12 13 14 15 16 17 18 19 1a 1b 1c 1d 1e 1f 0 1 2 3 4 5 6 7 8 9 a b c d e f 10 11 12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
  //   Control ROM
  //   contents of rom_2 (hex, n*v repeats v):
  //   0 11 8220 8420 8309 8305 10a1 704 702 9321 820 11a1 85 82 20040 140040 4604 24604 14004 14604 14204
endmodule

module bus_buffer (
  input  [15:0] Low_Address,
  input  [15:0] High_Address,
  input  [15:0] Address_Bus,
  output Select,
  output [15:0] Mapped_Address
);

  wire comparator_1_eq, comparator_1_gt, comparator_2_eq, comparator_2_lt, or_1_out, or_2_out;

  Subtractor #(.width(16)) subtractor_1 (.a(Address_Bus), .b(Low_Address), .out(Mapped_Address));  // open: bin, bout
  Comparator #(.width(16), .mode("unsigned")) comparator_1 (
    .a(Address_Bus), .b(Low_Address), .gt(comparator_1_gt), .eq(comparator_1_eq));  // open: lt
  and and_1 (Select, or_1_out, or_2_out);
  or or_1 (or_1_out, comparator_1_eq, comparator_1_gt);
  Comparator #(.width(16), .mode("unsigned")) comparator_2 (
    .a(Address_Bus), .b(High_Address), .eq(comparator_2_eq), .lt(comparator_2_lt));  // open: gt
  or or_2 (or_2_out, comparator_2_eq, comparator_2_lt);
endmodule
