// Logisim project cpu_known_good.circ as structural Verilog
module register_file (
  input  WRITE,
  input  [2:0] Sel_RD,
  input  [2:0] Sel_RS,
  input  [2:0] Sel_RT,
  input  [15:0] Data,
  input  CLK,
  output [15:0] RS,
  output [15:0] RT
);

  wire decoder_1_out0, decoder_1_out1, decoder_1_out2, decoder_1_out3, decoder_1_out4, decoder_1_out5,
       decoder_1_out6, decoder_1_out7;
  wire [15:0] register_1_q, register_2_q, register_3_q, register_4_q, register_5_q, register_6_q,
       register_7_q, register_8_q;

  Decoder #(.select(3), .disabled(0)) decoder_1 (
    .out0(decoder_1_out0), .out1(decoder_1_out1), .out2(decoder_1_out2), .out3(decoder_1_out3),
    .out4(decoder_1_out4), .out5(decoder_1_out5), .out6(decoder_1_out6), .out7(decoder_1_out7), .sel(Sel_RD),
    .en(WRITE));
  Register #(.width(16)) register_1 (.D(Data), .en(decoder_1_out0), .Q(register_1_q), .clk(CLK));  // open: clr
  Register #(.width(16)) register_2 (.D(Data), .en(decoder_1_out1), .Q(register_2_q), .clk(CLK));  // open: clr
  Register #(.width(16)) register_3 (.D(Data), .en(decoder_1_out2), .Q(register_3_q), .clk(CLK));  // open: clr
  Register #(.width(16)) register_4 (.D(Data), .en(decoder_1_out3), .Q(register_4_q), .clk(CLK));  // open: clr
  Register #(.width(16)) register_5 (.D(Data), .en(decoder_1_out4), .Q(register_5_q), .clk(CLK));  // open: clr
  Register #(.width(16)) register_6 (.D(Data), .en(decoder_1_out5), .Q(register_6_q), .clk(CLK));  // open: clr
  Register #(.width(16)) register_7 (.D(Data), .en(decoder_1_out6), .Q(register_7_q), .clk(CLK));  // open: clr
  Register #(.width(16)) register_8 (.D(Data), .en(decoder_1_out7), .Q(register_8_q), .clk(CLK));  // open: clr
  Multiplexer #(.select(3), .width(16), .enable("false")) multiplexer_1 (
    .in0(register_1_q), .in1(register_2_q), .in2(register_3_q), .in3(register_4_q), .in4(register_5_q),
    .in5(register_6_q), .in6(register_7_q), .in7(register_8_q), .out(RS), .sel(Sel_RS));
  Multiplexer #(.select(3), .width(16), .enable("false")) multiplexer_2 (
    .in0(register_1_q), .in1(register_2_q), .in2(register_3_q), .in3(register_4_q), .in4(register_5_q),
    .in5(register_6_q), .in6(register_7_q), .in7(register_8_q), .out(RT), .sel(Sel_RT));
endmodule

module ALU (
  input  [3:0] Operation,
  input  [15:0] A,
  input  [15:0] B,
  output [15:0] Q,
  output Zero
);

  wire [15:0] adder_1_out, and_1_out, not_1_out, not_2_out, or_1_out, shifter_1_out, shifter_2_out,
       subtractor_1_out, xor_1_out;

  Adder #(.width(16)) adder_1 (.a(A), .b(B), .out(adder_1_out), .cin(1'b0));  // open: cout
  Subtractor #(.width(16)) subtractor_1 (.a(A), .b(B), .out(subtractor_1_out), .bin(1'b0));  // open: bout
  assign and_1_out = A & B;  // AND_Gate and_1, 16 bits wide
  assign or_1_out = A | B;  // OR_Gate or_1, 16 bits wide
  assign xor_1_out = A ^ B;  // XOR_Gate xor_1, 16 bits wide
  Shifter #(.width(16)) shifter_1 (.in(A), .\dist (B[3:0]), .out(shifter_1_out));
  Shifter #(.width(16), .shift("lr")) shifter_2 (.in(A), .\dist (B[3:0]), .out(shifter_2_out));
  assign not_1_out = ~and_1_out;  // NOT_Gate not_1, 16 bits wide
  assign not_2_out = ~or_1_out;  // NOT_Gate not_2, 16 bits wide
  nor nor_1 (Zero, Q[15], Q[14], Q[13], Q[12], Q[11], Q[10], Q[9], Q[8], Q[6], Q[5], Q[4], Q[3], Q[2], Q[1], Q[0], Q[7]);
  Multiplexer #(.select(4), .width(16), .disabled(0), .enable("false")) multiplexer_1 (
    .in0(adder_1_out), .in1(subtractor_1_out), .in2(and_1_out), .in3(not_1_out), .in4(or_1_out),
    .in5(not_2_out), .in6(xor_1_out), .in8(shifter_1_out), .in9(shifter_2_out), .out(Q), .sel(Operation));  // open: in7, in10, in11, in12, in13, in14, in15

  // Notes on the sheet:
  //   B: pull=down
  //   Zero: pull=down
  //   Operation: pull=down
  //   Q: pull=down
  //   A: pull=down
endmodule

module CPU (
  input  CLK,
  input  [15:0] Address_Bus,
  input  [15:0] Data_Bus,
  output Read,
  output Write
);

  wire alu_1_zero, undriven_5, undriven_6, undriven_9, undriven_10, undriven_11, undriven_13;
  wire [1:0] undriven_7, undriven_8, undriven_12;
  wire [2:0] undriven_2, undriven_3, undriven_4;
  wire [3:0] undriven;
  wire [15:0] alu_1_q, controlled_buffer_1_out, IMM_q, IR_q, multiplexer_2_out, multiplexer_3_out,
       multiplexer_4_out, multiplexer_5_out, PC_q, register_file_1_rs, register_file_1_rt;

  Register #(.width(16)) IMM (.D(controlled_buffer_1_out), .en(undriven_10), .Q(IMM_q), .clk(CLK));  // open: clr
  Multiplexer #(.select(2), .width(16), .disabled(0), .enable("false")) multiplexer_1 (
    .in0(PC_q), .in1(register_file_1_rs), .in2(alu_1_q), .out(Address_Bus), .sel(undriven_8));  // open: in3
  Multiplexer #(.width(16), .disabled(0), .enable("false")) multiplexer_2 (
    .in0(controlled_buffer_1_out), .in1(IMM_q), .out(multiplexer_2_out), .sel(undriven_6));
  assign controlled_buffer_1_out = Read ? Data_Bus : 16'bz;  // Controlled_Buffer controlled_buffer_1
  assign Data_Bus = Write ? controlled_buffer_1_out : 16'bz;  // Controlled_Buffer controlled_buffer_2
  register_file register_file_1 (
    .Data(multiplexer_2_out), .RS(register_file_1_rs), .RT(register_file_1_rt), .WRITE(undriven_11),
    .Sel_RD(undriven_4), .Sel_RS(undriven_3), .Sel_RT(undriven_2), .CLK(CLK));
  Multiplexer #(.select(2), .width(16), .disabled(0), .enable("false")) multiplexer_3 (
    .in0(alu_1_q), .in1(register_file_1_rs), .in2(controlled_buffer_1_out), .in3(IMM_q),
    .out(multiplexer_3_out), .sel(undriven_12));
  Register #(.width(16)) IR (.D(controlled_buffer_1_out), .en(undriven_9), .Q(IR_q), .clk(CLK));  // open: clr
  Register #(.width(16)) PC (.D(multiplexer_3_out), .en(undriven_13), .Q(PC_q), .clk(CLK));  // open: clr
  Multiplexer #(.width(16), .disabled(0), .enable("false")) multiplexer_4 (
    .in0(register_file_1_rs), .in1(PC_q), .out(multiplexer_4_out), .sel(undriven_5));
  Multiplexer #(.select(2), .width(16), .disabled(0), .enable("false")) multiplexer_5 (
    .in0(register_file_1_rt), .in1(16'h1), .in2(16'h2), .in3(IMM_q), .out(multiplexer_5_out), .sel(undriven_7));
  ALU alu_1 (.A(multiplexer_4_out), .B(multiplexer_5_out), .Q(alu_1_q), .Operation(undriven), .Zero(alu_1_zero));

  // Notes on the sheet:
  //   Write: pull=down
  //   Read: pull=down
endmodule
